// Digital circuit CPU.dig as structural Verilog
module CPU (
  input  clk
);

  wire and_1_out, BranchHandler_jmp, CU_alumath, CU_branch, CU_fs, CU_immrs1, CU_immrs2, CU_jmpr, CU_load,
       CU_store, or_1_out;
  wire [1:0] CU_st;
  wire [3:0] ALU_z, register_1_q;
  wire [4:0] CU_operation, CU_rd, CU_rs1, CU_rs1a, CU_rs2, CU_rs2b, multiplexer_2_out, multiplexer_3_out,
       multiplexer_4_out;
  wire [5:0] CU_sa;
  wire [12:0] CU_rs1immval, CU_rs2immval;
  wire [17:0] CU_offset;
  wire [31:0] add_1_s, add_2_s, ALU_result, IFU_instr, IFU_pc, multiplexer_1_out, multiplexer_5_out,
       multiplexer_6_out, multiplexer_7_out, multiplexer_8_out, multiplexer_9_out, RegisterFile_rs1_data,
       RegisterFile_rs2_data, SLL_out, SRA_out, SRL_out;

  and and_1 (and_1_out, BranchHandler_jmp, CU_branch);
  IFU IFU (.clk(clk), .PC_Target(add_1_s), .PC_Src(and_1_out), .PC(IFU_pc), .Instr(IFU_instr));
  Add #(.Bits(32)) add_1 (.a(IFU_pc), .b(multiplexer_1_out), .c_i(1'b0), .s(add_1_s));  // open: c_o
  Multiplexer #(.Bits(32)) multiplexer_1 (
    .sel(CU_jmpr), .in_0({{14{1'b0}}, CU_offset}), .in_1(RegisterFile_rs1_data), .out(multiplexer_1_out));
  CU CU (
    .Instruction(IFU_instr), .Rd(CU_rd), .Rs1(CU_rs1), .Rs2(CU_rs2), .ST(CU_st), .SA(CU_sa), .FS(CU_fs),
    .Rs1ImmVal(CU_rs1immval), .Offset(CU_offset), .Rs2ImmVal(CU_rs2immval), .Rs1A(CU_rs1a), .Rs2B(CU_rs2b),
    .ImmRs2(CU_immrs2), .ImmRs1(CU_immrs1), .operation(CU_operation), .ALUMath(CU_alumath),
    .Branch(CU_branch), .Load(CU_load), .Store(CU_store), .JMPR(CU_jmpr));  // open: Opcode
  Multiplexer #(.Bits(5)) multiplexer_2 (.sel(CU_immrs1), .in_0(CU_rs2), .in_1(CU_rs2b), .out(multiplexer_2_out));
  Multiplexer #(.Bits(5)) multiplexer_3 (.sel(CU_immrs2), .in_0(CU_rs1), .in_1(CU_rs1a), .out(multiplexer_3_out));
  Multiplexer #(.Bits(5)) multiplexer_4 (
    .sel(CU_store), .in_0(multiplexer_2_out), .in_1(CU_rd), .out(multiplexer_4_out));
  BranchHandler BranchHandler (
    .funct(CU_operation), .Z(register_1_q[0]), .N(register_1_q[1]), .C(register_1_q[2]), .V(register_1_q[3]),
    .JMP(BranchHandler_jmp));
  Register #(.Bits(4)) register_1 (.D(ALU_z), .C(clk), .en(CU_fs), .Q(register_1_q));
  or or_1 (or_1_out, CU_immrs2, CU_immrs1);
  RAMDualPort #(.AddrBits(24), .Bits(32)) ramdualport_1 (
    .A(add_2_s[23:0]), .Din(RegisterFile_rs2_data), .str(CU_store), .C(clk), .ld(CU_load));  // open: D
  Add #(.Bits(32)) add_2 (
    .a({{19{1'b0}}, CU_rs2immval}), .b(RegisterFile_rs1_data), .c_i(1'b0), .s(add_2_s));  // open: c_o
  Multiplexer #(.Bits(32)) multiplexer_5 (
    .sel(CU_immrs1), .in_0(RegisterFile_rs1_data), .in_1({{19{1'b0}}, CU_rs1immval}), .out(multiplexer_5_out));
  RegisterFile RegisterFile (
    .Rs1(multiplexer_3_out), .Rs2(multiplexer_4_out), .Rd(CU_rd), .WD(multiplexer_9_out), .WE(CU_alumath),
    .Clk(clk), .Rs1_Data(RegisterFile_rs1_data), .Rs2_Data(RegisterFile_rs2_data));
  Multiplexer #(.Bits(32)) multiplexer_6 (
    .sel(CU_immrs2), .in_0(RegisterFile_rs2_data), .in_1({{19{1'b0}}, CU_rs2immval}), .out(multiplexer_6_out));
  ALU ALU (
    .A(multiplexer_5_out), .B(multiplexer_6_out), .ALU_Ctrl(CU_operation), .Result(ALU_result), .Z(ALU_z[0]),
    .N(ALU_z[1]), .C(ALU_z[2]), .V(ALU_z[3]));
  BarrelShifter #(.Bits(32)) SLL (.in(ALU_result), .shift(CU_sa), .out(SLL_out));
  BarrelShifter #(.Bits(32), .direction("right")) SRL (.in(ALU_result), .shift(CU_sa), .out(SRL_out));
  Multiplexer #(.Selector_Bits(2), .Bits(32)) multiplexer_7 (
    .sel(CU_st), .in_0(SRA_out), .in_1(SRL_out), .in_2(SLL_out), .in_3({32{1'b0}}), .out(multiplexer_7_out));
  Multiplexer #(.Bits(32)) multiplexer_8 (
    .sel(or_1_out), .in_0(multiplexer_7_out), .in_1(ALU_result), .out(multiplexer_8_out));
  Multiplexer #(.Bits(32)) multiplexer_9 (
    .sel(CU_jmpr), .in_0(multiplexer_8_out), .in_1(IFU_pc), .out(multiplexer_9_out));
  BarrelShifter #(.barrelShifterMode("arithmetic"), .Bits(32), .direction("right")) SRA (
    .in(ALU_result), .shift(CU_sa), .out(SRA_out));
endmodule
